# Fritzing sketch ders4 (saved by Fritzing 0.9.2b)
breadboards: 1

parts:
  Part1 = Arduino Uno (Rev3)
  R1 = Resistor [tolerance=±5% resistance=10k package=THT]
  LED1 = LED - 5mm [color="Red (633nm)" package="5 mm [THT]"]
  R2 = Resistor [tolerance=±5% resistance=330 package=THT]
  R3 = Resistor [tolerance=±5% resistance=330 package=THT]
  R4 = Resistor [tolerance=±5% resistance=330 package=THT]
  R5 = Resistor [tolerance=±5% resistance=330 package=THT]
  LED2 = LED - 5mm [color="Red (633nm)" package="5 mm [THT]"]
  LED3 = LED - 5mm [color="Red (633nm)" package="5 mm [THT]"]
  LED4 = LED - 5mm [color="Red (633nm)" package="5 mm [THT]"]
  R6 = Photocell (LDR) [package=THT]

nets:
  N1: Part1.A0, R1.Pin_1, R6.pin_1
  N2: Part1.D4, LED4.cathode
  N3: Part1.D5_PWM, LED3.cathode
  N4: Part1.D6_PWM, LED2.cathode
  N5: Part1.D7, LED1.cathode
  N6: Part1.3V3, R6.pin_0
  N7: Part1.GND, R1.Pin_0, R2.Pin_1, R3.Pin_1, R4.Pin_1, R5.Pin_1
  N8: LED1.anode, R2.Pin_0
  N9: R3.Pin_0, LED2.anode
  N10: R4.Pin_0, LED3.anode
  N11: R5.Pin_0, LED4.anode
