# Fritzing sketch buzzer+hcsr04 (saved by Fritzing 0.9.2b)
breadboards: 1

parts:
  Part1 = Arduino Uno (Rev3)
  Part2 = SRF05 Ultrasonic Rangefinder
  J1 = Piezo Speaker
  R1 = Resistor [tolerance=±5% resistance=330 package=THT]  # not connected

nets:
  N1: Part1.D8, J1.pin2
  N2: Part1.D6_PWM, Part2.Echo
  N3: Part1.D7, Part2.Trig
  5V: Part1.5V, Part2.VCC
  GND: Part1.GND, Part2.GND
